# Fritzing sketch Circuit_Diagram (saved by Fritzing 0.9.3b)

parts:
  ESP32Cam = ESP32 - CAM
  FTDI_Module = Adafruit FTDI Friend [part_number="Adafruit #284"]
  Program_Switch = SWITCH_SPDT [package=kps-1290]

nets:
  N1: ESP32Cam.GND#7, FTDI_Module.GND
  5V: ESP32Cam.5V, FTDI_Module.VCC
  N2: ESP32Cam.GPIO0, Program_Switch.P
  N3: ESP32Cam.GND#12, Program_Switch.O
  N4: ESP32Cam.GPIO3_/_RX, FTDI_Module.TX
  N5: ESP32Cam.GPIO1_/_TX, FTDI_Module.RX

notes:
  ESP32Cam / OV2640 Camera Sensor Used to capture images for face recognition.
  Enable Program Switch when uploading Code to ESP32Cam
  FTDI Module used for data transfer between Computer and ESP32Cam

custom parts:
  ESP32 - CAM: The ESP32-CAM has a very competitive small-size camera module that can operate independently as a minimum system with a footprint of only 27*40.5*4.5mm and a deep sleep current of up to 6mA.
  Adafruit FTDI Friend: Long gone are the days of parallel ports and serial ports. Now the USB port reigns supreme! But USB is hard, and you just want to transfer your every-day serial data from a microcontroller to computer. What now? Enter the FTDI Friend! The FTDI Friend is a tweaked out FTDI FT232RL chip adapter. Sure, like the well-known FTDI cable, it can provide power to your project and there are 4 signal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
